// Logisim project ca_offline_ floating_ _point_adder_ v2.circ as structural Verilog
module main (
  input  [15:0] in_1,
  input  [15:0] B,
  output [10:0] out_3,
  output [3:0] out_4,
  output out_5
);

  wire adder_1_cout, and_1_out, comparator_1_gt, multiplexer_2_out, multiplexer_3_out, multiplexer_9_out,
       multiplexer_10_out, not_1_out, not_2_out, or_1_out, subtractor_1_bout, subtractor_2_bout, xor_1_out;
  wire [3:0] adder_2_out, bit_extender_3_out, bitfinder_1_index, multiplexer_1_out, multiplexer_6_out,
       multiplexer_12_out, negator_1_out, subtractor_1_out, subtractor_3_out, subtractor_4_out;
  wire [10:0] adder_3_out, bit_extender_4_out, multiplexer_11_out, shifter_3_out;
  wire [11:0] adder_1_out, bit_extender_1_out, bit_extender_2_out, multiplexer_4_out, multiplexer_5_out,
       multiplexer_7_out, multiplexer_8_out, negator_2_out, shifter_1_out, shifter_2_out, subtractor_2_out;

  CONTROL_UNIT control_unit_1 ();
  Multiplexer #(.width(4)) multiplexer_1 (
    .in0(in_1[14:11]), .in1(B[14:11]), .out(multiplexer_1_out), .sel(subtractor_1_bout));  // open: en
  Subtractor #(.width(4)) subtractor_1 (
    .a(in_1[14:11]), .b(B[14:11]), .out(subtractor_1_out), .bout(subtractor_1_bout));  // open: bin
  assign bit_extender_1_out = {{1{1'b1}}, in_1[10:0]};  // Bit_Extender bit_extender_1
  assign bit_extender_2_out = {{1{1'b1}}, B[10:0]};  // Bit_Extender bit_extender_2
  Negator #(.width(4)) negator_1 (.in(subtractor_1_out), .out(negator_1_out));
  Multiplexer multiplexer_2 (
    .in0(in_1[15]), .in1(B[15]), .out(multiplexer_2_out), .sel(subtractor_1_bout));  // open: en
  Multiplexer multiplexer_3 (.in0(in_1[15]), .in1(B[15]), .out(multiplexer_3_out), .sel(not_1_out));  // open: en
  Multiplexer #(.width(12)) multiplexer_4 (
    .in0(bit_extender_1_out), .in1(bit_extender_2_out), .out(multiplexer_4_out), .sel(subtractor_1_bout));  // open: en
  Multiplexer #(.width(12)) multiplexer_5 (
    .in0(bit_extender_1_out), .in1(bit_extender_2_out), .out(multiplexer_5_out), .sel(not_1_out));  // open: en
  Multiplexer #(.width(4)) multiplexer_6 (
    .in0(subtractor_1_out), .in1(negator_1_out), .out(multiplexer_6_out), .sel(subtractor_1_bout));  // open: en
  not not_1 (not_1_out, subtractor_1_bout);
  Shifter #(.width(12), .shift("lr")) shifter_1 (
    .in(multiplexer_5_out), .\dist (multiplexer_6_out), .out(shifter_1_out));
  xor xor_1 (xor_1_out, multiplexer_2_out, multiplexer_3_out);
  Adder #(.width(12)) adder_1 (
    .a(multiplexer_4_out), .b(shifter_1_out), .out(adder_1_out), .cout(adder_1_cout));  // open: cin
  Subtractor #(.width(12)) subtractor_2 (
    .a(multiplexer_4_out), .b(shifter_1_out), .out(subtractor_2_out), .bout(subtractor_2_bout));  // open: bin
  Comparator #(.width(12), .mode("unsigned")) comparator_1 (
    .a(multiplexer_4_out), .b(shifter_1_out), .gt(comparator_1_gt));  // open: eq, lt
  Negator #(.width(12)) negator_2 (.in(subtractor_2_out), .out(negator_2_out));
  Multiplexer #(.width(12)) multiplexer_7 (
    .in0(subtractor_2_out), .in1(negator_2_out), .out(multiplexer_7_out), .sel(subtractor_2_bout));  // open: en
  Multiplexer #(.width(12)) multiplexer_8 (
    .in0(adder_1_out), .in1(multiplexer_7_out), .out(multiplexer_8_out), .sel(xor_1_out));  // open: en
  Multiplexer multiplexer_9 (
    .in0(adder_1_cout), .in1(subtractor_2_bout), .out(multiplexer_9_out), .sel(xor_1_out));  // open: en
  Multiplexer multiplexer_10 (
    .in0(multiplexer_2_out), .in1(multiplexer_3_out), .out(multiplexer_10_out), .sel(comparator_1_gt));  // open: en
  assign bit_extender_3_out = {{3{1'b0}}, multiplexer_9_out};  // Bit_Extender bit_extender_3
  Adder #(.width(4)) adder_2 (.a(bit_extender_3_out), .b(multiplexer_1_out), .out(adder_2_out));  // open: cin, cout
  and and_1 (and_1_out, multiplexer_8_out[0], multiplexer_9_out);
  Shifter #(.width(12), .shift("lr")) shifter_2 (
    .in(multiplexer_8_out), .\dist (bit_extender_3_out), .out(shifter_2_out));
  assign bit_extender_4_out = {{10{1'b0}}, and_1_out};  // Bit_Extender bit_extender_4
  or or_1 (or_1_out, shifter_2_out[11], multiplexer_9_out);
  Subtractor #(.width(4)) subtractor_3 (
    .a(adder_2_out), .b(subtractor_4_out), .out(subtractor_3_out));  // open: bin, bout
  Adder #(.width(11)) adder_3 (.a(bit_extender_4_out), .b(shifter_2_out[10:0]), .out(adder_3_out));  // open: cin, cout
  not not_2 (not_2_out, or_1_out);
  BitFinder #(.width(11), .\type ("high1")) bitfinder_1 (
    .in(shifter_2_out[10:0]), .index(bitfinder_1_index));  // open: found
  Shifter #(.width(11)) shifter_3 (.in(shifter_2_out[10:0]), .\dist (subtractor_4_out), .out(shifter_3_out));
  Subtractor #(.width(4)) subtractor_4 (.a(bitfinder_1_index), .b(4'b1011), .out(subtractor_4_out));  // open: bin, bout
  Multiplexer #(.width(11)) multiplexer_11 (
    .in0(adder_3_out), .in1(shifter_3_out), .out(multiplexer_11_out), .sel(not_2_out));  // open: en
  Multiplexer #(.width(4)) multiplexer_12 (
    .in0(adder_2_out), .in1(subtractor_3_out), .out(multiplexer_12_out), .sel(not_2_out));  // open: en

  // Notes on the sheet:
  //   exponent 
  //   shifter
  //   small alu c
  //   first sign
  //   second sign
  //   first frac
  //   second frac
  //   rightshifted second frac
  //   right shift
  //   Chekcing if two signs are same
  //   sum of fractions
  //   Carray bit after sum
  //   Output Sign Bit
  //   Right or 0 shifted value
  //   rounding
  //   choosing left shift or right shift
  //   chossing left or right shifted significant
endmodule
