// Logisim project ca_offline_ floating_ point_adder_ v1.circ as structural Verilog
module main (
  input  [15:0] in_1,
  input  [15:0] B
);

  wire adder_1_cout, comparator_1_gt, multiplexer_2_out, multiplexer_3_out, multiplexer_9_out,
       multiplexer_10_out, not_1_out, subtractor_1_bout, subtractor_2_bout, xor_1_out;
  wire [3:0] multiplexer_1_out, multiplexer_6_out, negator_1_out, subtractor_1_out;
  wire [11:0] adder_1_out, bit_extender_1_out, bit_extender_2_out, multiplexer_4_out, multiplexer_5_out,
       multiplexer_7_out, multiplexer_8_out, negator_2_out, shifter_1_out, subtractor_2_out;

  CONTROL_UNIT control_unit_1 ();
  Multiplexer #(.width(4)) multiplexer_1 (
    .in0(in_1[14:11]), .in1(B[14:11]), .out(multiplexer_1_out), .sel(subtractor_1_bout));  // open: en
  Subtractor #(.width(4)) subtractor_1 (
    .a(in_1[14:11]), .b(B[14:11]), .out(subtractor_1_out), .bout(subtractor_1_bout));  // open: bin
  assign bit_extender_1_out = {{1{1'b1}}, in_1[10:0]};  // Bit_Extender bit_extender_1
  assign bit_extender_2_out = {{1{1'b1}}, B[10:0]};  // Bit_Extender bit_extender_2
  Negator #(.width(4)) negator_1 (.in(subtractor_1_out), .out(negator_1_out));
  Multiplexer multiplexer_2 (
    .in0(in_1[15]), .in1(B[15]), .out(multiplexer_2_out), .sel(subtractor_1_bout));  // open: en
  Multiplexer multiplexer_3 (.in0(in_1[15]), .in1(B[15]), .out(multiplexer_3_out), .sel(not_1_out));  // open: en
  Multiplexer #(.width(12)) multiplexer_4 (
    .in0(bit_extender_1_out), .in1(bit_extender_2_out), .out(multiplexer_4_out), .sel(subtractor_1_bout));  // open: en
  Multiplexer #(.width(12)) multiplexer_5 (
    .in0(bit_extender_1_out), .in1(bit_extender_2_out), .out(multiplexer_5_out), .sel(not_1_out));  // open: en
  Multiplexer #(.width(4)) multiplexer_6 (
    .in0(subtractor_1_out), .in1(negator_1_out), .out(multiplexer_6_out), .sel(subtractor_1_bout));  // open: en
  not not_1 (not_1_out, subtractor_1_bout);
  Shifter #(.width(12)) shifter_1 (.in(multiplexer_5_out), .\dist (multiplexer_6_out), .out(shifter_1_out));
  xor xor_1 (xor_1_out, multiplexer_2_out, multiplexer_3_out);
  Adder #(.width(12)) adder_1 (
    .a(multiplexer_4_out), .b(shifter_1_out), .out(adder_1_out), .cout(adder_1_cout));  // open: cin
  Subtractor #(.width(12)) subtractor_2 (
    .a(multiplexer_4_out), .b(shifter_1_out), .out(subtractor_2_out), .bout(subtractor_2_bout));  // open: bin
  Comparator #(.width(12), .mode("unsigned")) comparator_1 (
    .a(multiplexer_4_out), .b(shifter_1_out), .gt(comparator_1_gt));  // open: eq, lt
  Negator #(.width(12)) negator_2 (.in(subtractor_2_out), .out(negator_2_out));
  Multiplexer #(.width(12)) multiplexer_7 (
    .in0(subtractor_2_out), .in1(negator_2_out), .out(multiplexer_7_out), .sel(subtractor_2_bout));  // open: en
  Multiplexer #(.width(12)) multiplexer_8 (
    .in0(adder_1_out), .in1(multiplexer_7_out), .out(multiplexer_8_out), .sel(xor_1_out));  // open: en
  Multiplexer multiplexer_9 (
    .in0(adder_1_cout), .in1(subtractor_2_bout), .out(multiplexer_9_out), .sel(xor_1_out));  // open: en
  Multiplexer multiplexer_10 (
    .in0(multiplexer_2_out), .in1(multiplexer_3_out), .out(multiplexer_10_out), .sel(comparator_1_gt));  // open: en

  // Notes on the sheet:
  //   exponent 
  //   shifter
  //   small alu c
  //   first sign
  //   second sign
  //   first frac
  //   second frac
  //   rightshifted second frac
  //   right shift
  //   sum of fractions
  //   Carray bit after sum
  //   Output Sign Bit
endmodule
